# Fritzing sketch HC-SR04_ESP32 (saved by Fritzing 0.9.9b)

parts:
  M1 = DOIT Esp32 DevKit v1 (30 pins long, 11 pins width) [part_number=ESP32S-PIN30]
  HC-SR04_Sensor_1 = HC-SR04 Ultrasonic Distance Sensor

nets:
  N1: M1.D2, HC-SR04_Sensor_1.TRIG
  N2: M1.D4, HC-SR04_Sensor_1.ECHO
  GND: M1.GND, HC-SR04_Sensor_1.GND
  VIN: M1.VIN, HC-SR04_Sensor_1.VCC

notes:
  Vcc and Gnd must be connected with VIN and GND

custom parts:
  DOIT Esp32 DevKit v1 (30 pins long, 11 pins width): The DOIT Esp32 DevKit v1 is one of the development board created by DOIT to evaluate the ESP-WROOM-32 module. It is based on the ESP32 microcontroller that boasts Wifi, Bluetooth, Ethernet and Low Power support all in a single chip. (vanepp) made breadboard work, adjusted pin numbering and labels and reduced size of schematic and cleaned up pcb. This chip is 30pins long (2 x15) and 11 pins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
