# Fritzing sketch SG90_Arduino (saved by Fritzing 0.9.9b)

parts:
  Part1 = Arduino Uno (Rev3)
  J1 = Basic Servo

nets:
  N1: Part1.D9_PWM, J1.pulse
  5V: Part1.5V, J1.vcc
  GND: Part1.GND, J1.gnd

notes:
  5v =
  5v
  GND =
  Control =
  red
  black/
  brown
  orange/
  yellow
